// Logisim project control-logic.circ as structural Verilog: 1 circuit, main circuit control_logic
module control_logic (
  input  [31:0] inst,
  input  BrEq,
  input  BrLt,
  input  [3:0] in_4,
  output PCSel,
  output RegWEn,
  output [2:0] ImmSel,
  output BrUn,
  output ASel,
  output BSel,
  output [3:0] ALUSel,
  output MemRW,
  output [1:0] WBSel,
  output CSRSel,
  output CSRWen
);

  wire op0_0_out, op0_1_out, op0_out;

  and op0_0 (op0_0_out, ~inst[4], ~inst[3]);  // AND_Gate
  and op1 (ImmSel[1], ~inst[3], inst[5]);  // AND_Gate
  and op0_1 (op0_1_out, op0_0_out, inst[6]);
  and op0 (op0_out, inst[4], ~inst[6]);  // AND_Gate
  or or_1 (ImmSel[0], op0_1_out, op0_out);
  // Probe on {inst[3], ImmSel[1:0]}

  assign ALUSel = in_4;
  assign BSel = 1'b1;
  assign ImmSel[2] = inst[3];
  assign RegWEn = 1'b1;

  // Notes on the sheet:
  //   INPUTS to your circuit
  //   ImmSel generator logic
  //   DON'T CHANGE THE LOCATIONS OF THE INPUTS AND OUTPUTS!
  //   OUTPUT from your circuit
endmodule
